# Fritzing sketch ARDUINO328AU (saved by Fritzing 0.8.7b)
breadboards: 1

parts:
  Part1 = Arduino Uno (Rev3)
  IC1 = TQFP32-5MM [chip_label=IC package=TQFP]
  XTAL1 = Crystal [frequency="16 Mhz" package=THT]
  C1 = Electrolytic Capacitor [capacitance=20µF package="0605 [SMD, electrolytic]"]
  C2 = Electrolytic Capacitor [capacitance=20µF package="0605 [SMD, electrolytic]"]
  C3 = Electrolytic Capacitor [capacitance=47µF package="0605 [SMD, electrolytic]"]
  R1 = Resistor [tolerance=±5% resistance=120 package=THT]

nets:
  N1: Part1.D10_PWM/SS, IC1.32, R1.Pin_1
  N2: Part1.D11_PWM/MOSI, IC1.12
  N3: Part1.D12/MISO, IC1.13
  N4: Part1.D13/SCK, IC1.20
  N5: Part1.GND, IC1.2, IC1.23, IC1.24, C1.-, C2.-, C3.-, C3.+
  N6: IC1.1, IC1.3, IC1.21, R1.Pin_0
  N7: IC1.4, XTAL1.pin_1, C1.+
  N8: IC1.5, XTAL1.pin_0

notes:
  Atmega328-AU
